// Logisim project schaltung.circ as structural Verilog: 1 circuit, main circuit main
module main (
  input  E3,
  input  E2,
  input  E1,
  output A1
);

  wire and_1_out, and_2_out, nor_1_out, not_1_out;

  not not_1 (not_1_out, E2);
  nor nor_1 (nor_1_out, E1, E2, E3);
  and and_1 (and_1_out, E1, not_1_out, E3);
  and and_2 (and_2_out, E1, E3);
  or or_1 (A1, nor_1_out, and_1_out, and_2_out);
endmodule
